// Digital circuit procesor.dig as structural Verilog
module procesor (
  input  in_1,
  input  in_2,
  input  in_3,
  input  in_4,
  input  in_5,
  input  in_6,
  input  in_7,
  input  in_8,
  input  in_9,
  input  in_10,
  input  in_11,
  input  in_12,
  input  in_13,
  input  in_14,
  input  in_15,
  input  in_16,
  input  in_17,
  input  in_18,
  input  in_19,
  input  in_20,
  input  in_21,
  input  in_22,
  input  in_23,
  input  in_24,
  input  in_25,
  input  in_26,
  input  in_27,
  input  in_28,
  input  in_29,
  input  in_30,
  input  in_31,
  input  in_32,
  input  in_33
);

  wire _16bite_sumator_1_out1, _16bite_sumator_1_out2, _16bite_sumator_1_out3, _16bite_sumator_1_out4,
       _16bite_sumator_1_out5, _16bite_sumator_1_out6, _16bite_sumator_1_out7, _16bite_sumator_1_out8,
       _16bite_sumator_1_out9, _16bite_sumator_1_out10, _16bite_sumator_1_out11, _16bite_sumator_1_out12,
       _16bite_sumator_1_out13, _16bite_sumator_1_out14, _16bite_sumator_1_out15, _16bite_sumator_1_out16,
       _16bite_sumator_1_out_cary, multiplexor_1_couta, multiplexor_2_couta, multiplexor_3_couta,
       multiplexor_4_couta, multiplexor_5_couta, multiplexor_6_couta, multiplexor_7_couta,
       multiplexor_8_couta, multiplexor_9_couta, multiplexor_10_couta, multiplexor_11_couta,
       multiplexor_12_couta, multiplexor_13_couta, multiplexor_14_couta, multiplexor_15_couta,
       multiplexor_16_couta;

  multiplexor multiplexor_1 (.CinA(in_25), .Cin_com(in_33), .CoutA(multiplexor_1_couta));
  multiplexor multiplexor_2 (.CinA(in_26), .Cin_com(in_33), .CoutA(multiplexor_2_couta));
  multiplexor multiplexor_3 (.CinA(in_27), .Cin_com(in_33), .CoutA(multiplexor_3_couta));
  multiplexor multiplexor_4 (.CinA(in_28), .Cin_com(in_33), .CoutA(multiplexor_4_couta));
  multiplexor multiplexor_5 (.CinA(in_29), .Cin_com(in_33), .CoutA(multiplexor_5_couta));
  multiplexor multiplexor_6 (.CinA(in_30), .Cin_com(in_33), .CoutA(multiplexor_6_couta));
  multiplexor multiplexor_7 (.CinA(in_31), .Cin_com(in_33), .CoutA(multiplexor_7_couta));
  multiplexor multiplexor_8 (.CinA(in_32), .Cin_com(in_33), .CoutA(multiplexor_8_couta));
  multiplexor multiplexor_9 (.CinA(in_17), .Cin_com(in_33), .CoutA(multiplexor_9_couta));
  multiplexor multiplexor_10 (.CinA(in_18), .Cin_com(in_33), .CoutA(multiplexor_10_couta));
  multiplexor multiplexor_11 (.CinA(in_19), .Cin_com(in_33), .CoutA(multiplexor_11_couta));
  multiplexor multiplexor_12 (.CinA(in_20), .Cin_com(in_33), .CoutA(multiplexor_12_couta));
  multiplexor multiplexor_13 (.CinA(in_21), .Cin_com(in_33), .CoutA(multiplexor_13_couta));
  multiplexor multiplexor_14 (.CinA(in_22), .Cin_com(in_33), .CoutA(multiplexor_14_couta));
  multiplexor multiplexor_15 (.CinA(in_23), .Cin_com(in_33), .CoutA(multiplexor_15_couta));
  multiplexor multiplexor_16 (.CinA(in_24), .Cin_com(in_33), .CoutA(multiplexor_16_couta));
  LED led_1 (.in(_16bite_sumator_1_out1));
  LED led_2 (.in(_16bite_sumator_1_out2));
  LED led_3 (.in(_16bite_sumator_1_out3));
  LED led_4 (.in(_16bite_sumator_1_out4));
  LED led_5 (.in(_16bite_sumator_1_out5));
  LED led_6 (.in(_16bite_sumator_1_out6));
  LED led_7 (.in(_16bite_sumator_1_out7));
  LED led_8 (.in(_16bite_sumator_1_out8));
  LED led_9 (.in(_16bite_sumator_1_out9));
  LED led_10 (.in(_16bite_sumator_1_out10));
  LED led_11 (.in(_16bite_sumator_1_out11));
  LED led_12 (.in(_16bite_sumator_1_out12));
  LED led_13 (.in(_16bite_sumator_1_out13));
  LED led_14 (.in(_16bite_sumator_1_out14));
  LED led_15 (.in(_16bite_sumator_1_out15));
  LED led_16 (.in(_16bite_sumator_1_out16));
  LED led_17 (.in(_16bite_sumator_1_out_cary));
  _16bite_sumator _16bite_sumator_1 (
    .B16(in_9), .B15(in_10), .B14(in_11), .B13(in_12), .B12(in_13), .B11(in_14), .B10(in_15), .B9(in_16),
    .B8(in_1), .B7(in_2), .B6(in_3), .B5(in_4), .B4(in_5), .B3(in_6), .B2(in_7), .B1(in_8),
    .A16(multiplexor_8_couta), .A15(multiplexor_7_couta), .A14(multiplexor_6_couta),
    .A13(multiplexor_5_couta), .A12(multiplexor_4_couta), .A11(multiplexor_3_couta),
    .A10(multiplexor_2_couta), .A9(multiplexor_1_couta), .A8(multiplexor_16_couta),
    .A7(multiplexor_15_couta), .A6(multiplexor_14_couta), .A5(multiplexor_13_couta),
    .A4(multiplexor_12_couta), .A3(multiplexor_11_couta), .A2(multiplexor_10_couta),
    .A1(multiplexor_9_couta), .Cary(in_33), .Out_cary(_16bite_sumator_1_out_cary),
    .Out16(_16bite_sumator_1_out16), .Out15(_16bite_sumator_1_out15), .Out14(_16bite_sumator_1_out14),
    .Out13(_16bite_sumator_1_out13), .Out12(_16bite_sumator_1_out12), .Out11(_16bite_sumator_1_out11),
    .Out10(_16bite_sumator_1_out10), .Out9(_16bite_sumator_1_out9), .Out8(_16bite_sumator_1_out8),
    .Out7(_16bite_sumator_1_out7), .Out6(_16bite_sumator_1_out6), .Out5(_16bite_sumator_1_out5),
    .Out4(_16bite_sumator_1_out4), .Out3(_16bite_sumator_1_out3), .Out2(_16bite_sumator_1_out2),
    .Out1(_16bite_sumator_1_out1));
endmodule
